# Fritzing sketch weatherpi (saved by Fritzing 0.9.1b)

parts:
  Raspberry_Pi1 = Raspberry Pi B+
  RHT1 = Humidity and Temperature Sensor RHT03
  R1 = Resistor [tolerance=±5% resistance=220 package=THT]
  JP1 = Header 4 [package=jst-4-pth]

nets:
  N1: Raspberry_Pi1.GPIO2, JP1.4
  N2: Raspberry_Pi1.GPIO3, JP1.3
  N3: Raspberry_Pi1.GPIO4, RHT1.Data-signal, R1.Pin_1
  N4: Raspberry_Pi1.GND, RHT1.GND_2, JP1.2
  N5: RHT1.Vcc, R1.Pin_0, JP1.1

notes:
  BMP180
  VIN|GND|SCL|SDA
